# Fritzing sketch IR LED Connection (saved by Fritzing 1.0.5)
breadboards: 1

parts:
  MCU1 = Raspberry Pi Zero
  R1 = Resistor [tolerance=±5% power=0.25W resistance=220 package=THT]
  LED1 = LED - 5mm [color="Infrared (880nm)" current=0.030A package="5 mm [THT]"]

nets:
  N1: MCU1.pin_6, LED1.cathode
  N2: MCU1.pin_8, R1.Pin_1
  N3: R1.Pin_0, LED1.anode
